# Fritzing sketch Blinky-Button (saved by Fritzing 0.9.2b)
breadboards: 1

parts:
  Part1 = Arduino Uno (Rev3)
  LED1 = LED - 5mm [color="Red (633nm)" package="5 mm [THT]"]
  S1 = Pushbutton [package="[THT]"]

nets:
  N1: Part1.D8, Part1.5V, S1.Pin_1, S1.Pin_2
  N2: Part1.D13/SCK, LED1.anode
  N3: Part1.GND, LED1.cathode
  N4: S1.Pin_3, S1.Pin_4
